# Fritzing sketch museDash (saved by Fritzing 0.9.4)
breadboards: 1

parts:
  R1 = Resistor [tolerance=±5% resistance=100k package=THT]
  C1 = Ceramic Capacitor [capacitance=100nF package="100 mil [THT, multilayer]"]
  S1 = Pushbutton [package=THT]
  switch1 = Toggle Switch [package=THT]
  IC2 = Hex Inverter Schmitt Trigger SN74HC14 [package="DIP (Dual Inline)"]
  R2 = Resistor [tolerance=±5% resistance=100k package=THT]
  R3 = Resistor [tolerance=±5% resistance=100k package=THT]
  R4 = Resistor [tolerance=±5% resistance=100k package=THT]
  C2 = Ceramic Capacitor [capacitance=100nF package="100 mil [THT, multilayer]"]
  S2 = Pushbutton [package=THT]
  R5 = Resistor [tolerance=±5% resistance=100k package=THT]
  R6 = Resistor [tolerance=±5% resistance=100k package=THT]
  C3 = Ceramic Capacitor [capacitance=100nF package="100 mil [THT, multilayer]"]
  S3 = Pushbutton [package=THT]
  R7 = Resistor [tolerance=±5% resistance=100k package=THT]
  C4 = Ceramic Capacitor [capacitance=100nF package="100 mil [THT, multilayer]"]
  S4 = Pushbutton [package=THT]
  R8 = Resistor [tolerance=±5% resistance=100k package=THT]
  CONN1 = USB connector [package=THT]  # not connected
  Компонент1 = Arduino Micro (Rev3)
  CD_4017 = IC, DIP package, 16 pins [chip_label=IC]
  D1 = Rectifier Diode [part_number=1N4001 package="300 mil [THT]"]
  S5 = Pushbutton [package=THT]
  R9 = Resistor [tolerance=±5% resistance=4.7k package=THT]
  D2 = Rectifier Diode [part_number=1N4001 package="300 mil [THT]"]
  S6 = Pushbutton [package=THT]
  D3 = Rectifier Diode [part_number=1N4001 package="300 mil [THT]"]
  D4 = Rectifier Diode [part_number=1N4001 package="300 mil [THT]"]
  S7 = Pushbutton [package=THT]
  S8 = Pushbutton [package=THT]
  D5 = Rectifier Diode [part_number=1N4001 package="300 mil [THT]"]
  D6 = Rectifier Diode [part_number=1N4001 package="300 mil [THT]"]
  D7 = Rectifier Diode [part_number=1N4001 package="300 mil [THT]"]
  D8 = Rectifier Diode [part_number=1N4001 package="300 mil [THT]"]
  S9 = Pushbutton [package=THT]
  S10 = Pushbutton [package=THT]
  S11 = Pushbutton [package=THT]
  S12 = Pushbutton [package=THT]

nets:
  N1: R1.Pin_0, S1.leg1, R2.Pin_1
  N2: R1.Pin_1, C1.1, IC2.1A
  GND: C1.0, S1.leg0, switch1.L2, IC2.GND, C2.0, S2.leg0, C3.0, S3.leg0, S4.leg0, Компонент1.GND, CD_4017.pin8, R9.Pin_1
  5V: switch1.L1, IC2.VCC, R2.Pin_0, R4.Pin_0, R6.Pin_1, R8.Pin_1, CD_4017.pin16
  N3: switch1.COM, Компонент1.D13_PWM
  N4: IC2.1Y, Компонент1.D1/TX, Компонент1.D5_PWM
  N5: IC2.2A, R3.Pin_1, C2.1
  N6: IC2.2Y, Компонент1.D0/RX, Компонент1.D4_PWM/A6
  N7: IC2.5Y, Компонент1.D3/SCL, Компонент1.D8_PWM/A8
  N8: IC2.5A, R5.Pin_0, C3.1
  N9: IC2.6Y, Компонент1.D2/SDA, Компонент1.D6_PWM/A7
  N10: IC2.6A, R7.Pin_0, C4.1
  N11: R3.Pin_0, R4.Pin_1, S2.leg1
  N12: R5.Pin_1, R6.Pin_0, S3.leg1
  N13: R7.Pin_1, S4.leg1, R8.Pin_0
  N14: Компонент1.D7, S5.leg1, R9.Pin_0, S6.leg1, S7.leg1, S8.leg1, S9.leg1, S10.leg1, S11.leg1, S12.leg1
  N15: Компонент1.D9_PWM/A9, CD_4017.pin13
  N16: Компонент1.D10_PWM/A10, CD_4017.pin14
  N17: Компонент1.D11_PWM, CD_4017.pin15
  N18: CD_4017.pin1, D1.anode
  N19: CD_4017.pin2, D2.anode
  N20: CD_4017.pin3, D3.anode
  N21: CD_4017.pin4, D4.anode
  N22: CD_4017.pin5, D5.anode
  N23: CD_4017.pin6, D8.anode
  N24: CD_4017.pin7, D7.anode
  N25: CD_4017.pin10, D6.anode
  N26: D1.cathode, S5.leg0
  N27: D2.cathode, S6.leg0
  N28: D3.cathode, S7.leg0
  N29: D4.cathode, S8.leg0
  N30: D5.cathode, S9.leg0
  N31: D6.cathode, S10.leg0
  N32: D7.cathode, S12.leg0
  N33: D8.cathode, S11.leg0

notes:
  Mod
  (initialized at power on)
  Game Buttons
  Y, B, A, L
  +, -, HOME, LEFT, RIGHT, UP, DOWN
